# Fritzing sketch control_board_pcb (saved by Fritzing 0.9.2b)
circuit board: 7cm x 7cm
breadboards: 1

parts:
  S2 = SWITCH-MOMENTARY-2 [package=tactile-pth-12mm]
  S3 = Momentary Switch [package=tactile-pth]
  S4 = Momentary Switch [package=tactile-pth]
  S5 = Momentary Switch [package=tactile-pth]
  S6 = Momentary Switch [package=tactile-pth]
  S7 = Momentary Switch [package=tactile-pth]
  S8 = Momentary Switch [package=tactile-pth]
  S9 = Momentary Switch [package=tactile-pth]
  S10 = Momentary Switch [package=tactile-pth]
  LED1 = LED - 3mm [color="Red (633nm)" package="3 mm [THT]"]
  LED2 = LED - 3mm [color="Red (633nm)" package="3 mm [THT]"]
  R1 = Resistor [tolerance=±5% resistance=220 package=THT]

nets:
  N1: S2.2, S4.1
  N2: S3.4, S4.2, S5.1, S6.3
  N3: S6.4, R1.Pin_0
  N4: S7.3, S8.4, S9.4
  N5: S9.3, S10.4
  N6: LED1.anode, LED2.anode, R1.Pin_1
